// Digital circuit adder-logic.dig as structural Verilog
module adder_logic (
  input  B_0,
  input  B_1,
  input  B_2,
  input  B_3,
  input  A_0,
  input  A_1,
  input  A_2,
  input  A_3
);

  wire _74283_1_pin1, _74283_1_pin4, _74283_1_pin9, _74283_1_pin10, _74283_1_pin13;

  _74283 _74283_1 (
    .pin1(_74283_1_pin1), .pin2(B_1), .pin3(A_1), .pin4(_74283_1_pin4), .pin5(A_0), .pin6(B_0), .pin7(1'b0),
    .pin8(1'b0), .pin9(_74283_1_pin9), .pin10(_74283_1_pin10), .pin11(B_3), .pin12(A_3),
    .pin13(_74283_1_pin13), .pin14(A_2), .pin15(B_2), .pin16(1'b1));
  LED S_0 (.in(_74283_1_pin4));
  LED S_1 (.in(_74283_1_pin1));
  LED S_2 (.in(_74283_1_pin13));
  LED S_3 (.in(_74283_1_pin10));
  LED C_out (.in(_74283_1_pin9));
endmodule
