// Digital circuit adder-real.dig as structural Verilog
module adder_real (
);

  wire _74283_1_pin1, _74283_1_pin4, _74283_1_pin9, _74283_1_pin10, _74283_1_pin13, A_0_b, A_1_b, A_2_b,
       A_3_b, B_0_b, B_1_b, B_2_b, B_3_b;

  Switch A_0 (.A(1'b0), .B(A_0_b));
  Switch A_1 (.A(1'b0), .B(A_1_b));
  Switch A_2 (.A(1'b0), .B(A_2_b));
  Switch A_3 (.A(1'b0), .B(A_3_b));
  Switch B_0 (.A(1'b0), .B(B_0_b));
  Switch B_1 (.A(1'b0), .B(B_1_b));
  Switch B_2 (.A(1'b0), .B(B_2_b));
  Switch B_3 (.A(1'b0), .B(B_3_b));
  PullUp pullup_1 (.out(A_0_b));
  PullUp pullup_2 (.out(A_1_b));
  PullUp pullup_3 (.out(B_0_b));
  PullUp pullup_4 (.out(B_1_b));
  PullUp pullup_5 (.out(A_2_b));
  PullUp pullup_6 (.out(A_3_b));
  PullUp pullup_7 (.out(B_2_b));
  PullUp pullup_8 (.out(B_3_b));
  _74283 _74283_1 (
    .pin1(_74283_1_pin1), .pin2(B_1_b), .pin3(A_1_b), .pin4(_74283_1_pin4), .pin5(A_0_b), .pin6(B_0_b),
    .pin7(1'b0), .pin8(1'b0), .pin9(_74283_1_pin9), .pin10(_74283_1_pin10), .pin11(B_3_b), .pin12(A_3_b),
    .pin13(_74283_1_pin13), .pin14(A_2_b), .pin15(B_2_b), .pin16(1'b1));
  LED S_0 (.in(_74283_1_pin4));
  LED S_1 (.in(_74283_1_pin1));
  LED S_2 (.in(_74283_1_pin13));
  LED S_3 (.in(_74283_1_pin10));
  LED C_out (.in(_74283_1_pin9));
endmodule
