// Digital circuit alu-nand-mux.dig as structural Verilog
module alu_nand_mux (
);

  wire _7486_1_pin3, _7486_1_pin6, _7486_1_pin8, _7486_1_pin11, _74257_1_pin4, _74257_1_pin7, _74257_1_pin9,
       _74257_1_pin12, _74283_1_pin9, a_0, a_1, a_2, a_3, b_0, b_1, b_2, b_3, Enablemux, nand_1, nand_2,
       nand_3, nand_4, sub, sum_1, sum_2, sum_3, sum_4;

  LED m_3 (.in(_74257_1_pin12));
  LED m_2 (.in(_74257_1_pin9));
  LED m_1 (.in(_74257_1_pin7));
  LED m_0 (.in(_74257_1_pin4));
  _74257 _74257_1 (
    .pin1(Enablemux), .pin2(sum_1), .pin3(nand_1), .pin4(_74257_1_pin4), .pin5(sum_2), .pin6(nand_2),
    .pin7(_74257_1_pin7), .pin8(1'b0), .pin9(_74257_1_pin9), .pin10(nand_3), .pin11(sum_3),
    .pin12(_74257_1_pin12), .pin13(nand_4), .pin14(sum_4), .pin15(1'b0), .pin16(1'b1));
  PullUp pullup_1 (.out(Enablemux));
  Switch #(.Closed("true")) switch_1 (.A(1'b0), .B(Enablemux));
  LED y_3 (.in(nand_4));
  LED y_2 (.in(nand_3));
  Switch #(.Closed("true")) u_a_0 (.A(1'b0), .B(a_0));
  Switch #(.Closed("true")) u_a_1 (.A(1'b0), .B(a_1));
  Switch #(.Closed("true")) u_a_2 (.A(1'b0), .B(a_2));
  Switch #(.Closed("true")) u_a_3 (.A(1'b0), .B(a_3));
  Switch #(.Closed("true")) u_b_0 (.A(1'b0), .B(b_0));
  Switch #(.Closed("true")) u_b_1 (.A(1'b0), .B(b_1));
  Switch #(.Closed("true")) u_b_2 (.A(1'b0), .B(b_2));
  Switch #(.Closed("true")) u_b_3 (.A(1'b0), .B(b_3));
  Switch #(.Closed("true")) u_sub (.A(1'b0), .B(sub));
  LED y_0 (.in(nand_1));
  LED y_1 (.in(nand_2));
  PullUp pullup_2 (.out(a_0));
  PullUp pullup_3 (.out(b_0));
  PullUp pullup_4 (.out(a_2));
  PullUp pullup_5 (.out(a_1));
  PullUp pullup_6 (.out(b_2));
  PullUp pullup_7 (.out(b_1));
  PullUp pullup_8 (.out(a_3));
  PullUp pullup_9 (.out(b_3));
  PullUp pullup_10 (.out(sub));
  _7400 _7400_1 (
    .pin1(a_0), .pin2(b_0), .pin3(nand_1), .pin4(a_1), .pin5(b_1), .pin6(nand_2), .pin7(1'b0), .pin8(nand_3),
    .pin9(a_2), .pin10(b_2), .pin11(nand_4), .pin12(a_3), .pin13(b_3), .pin14(1'b1));
  _7486 _7486_1 (
    .pin1(b_0), .pin2(sub), .pin3(_7486_1_pin3), .pin4(b_1), .pin5(sub), .pin6(_7486_1_pin6), .pin7(1'b0),
    .pin8(_7486_1_pin8), .pin9(b_2), .pin10(sub), .pin11(_7486_1_pin11), .pin12(b_3), .pin13(sub),
    .pin14(1'b1));
  _74283 _74283_1 (
    .pin1(sum_2), .pin2(_7486_1_pin6), .pin3(a_1), .pin4(sum_1), .pin5(a_0), .pin6(_7486_1_pin3), .pin7(sub),
    .pin8(1'b0), .pin9(_74283_1_pin9), .pin10(sum_4), .pin11(_7486_1_pin11), .pin12(a_3), .pin13(sum_3),
    .pin14(a_2), .pin15(_7486_1_pin8), .pin16(1'b1));
  LED S_0 (.in(sum_1));
  LED S_1 (.in(sum_2));
  LED S_2 (.in(sum_3));
  LED S_3 (.in(sum_4));
  LED C_out (.in(_74283_1_pin9));
endmodule
