// Digital circuit subadder-real.dig as structural Verilog
module subadder_real (
);

  wire _7486_1_pin3, _7486_1_pin6, _7486_1_pin8, _7486_1_pin11, _74283_1_pin1, _74283_1_pin4, _74283_1_pin9,
       _74283_1_pin10, _74283_1_pin13, a_0_b, a_1_b, a_2_b, a_3_b, b_0_b, b_1_b, b_2_b, b_3_b, sub_b;

  Switch #(.Closed("true")) a_0 (.A(1'b0), .B(a_0_b));
  Switch #(.Closed("true")) a_1 (.A(1'b0), .B(a_1_b));
  Switch #(.Closed("true")) a_2 (.A(1'b0), .B(a_2_b));
  Switch #(.Closed("true")) a_3 (.A(1'b0), .B(a_3_b));
  Switch #(.Closed("true")) b_0 (.A(1'b0), .B(b_0_b));
  Switch #(.Closed("true")) b_1 (.A(1'b0), .B(b_1_b));
  Switch #(.Closed("true")) b_2 (.A(1'b0), .B(b_2_b));
  Switch #(.Closed("true")) b_3 (.A(1'b0), .B(b_3_b));
  Switch #(.Closed("true")) sub (.A(1'b0), .B(sub_b));
  PullUp pullup_1 (.out(a_1_b));
  PullUp pullup_2 (.out(a_0_b));
  PullUp pullup_3 (.out(b_1_b));
  PullUp pullup_4 (.out(b_0_b));
  PullUp pullup_5 (.out(sub_b));
  PullUp pullup_6 (.out(a_3_b));
  PullUp pullup_7 (.out(a_2_b));
  PullUp pullup_8 (.out(b_3_b));
  PullUp pullup_9 (.out(b_2_b));
  _7486 _7486_1 (
    .pin1(b_0_b), .pin2(sub_b), .pin3(_7486_1_pin3), .pin4(b_1_b), .pin5(sub_b), .pin6(_7486_1_pin6),
    .pin7(1'b0), .pin8(_7486_1_pin8), .pin9(b_2_b), .pin10(sub_b), .pin11(_7486_1_pin11), .pin12(b_3_b),
    .pin13(sub_b), .pin14(1'b1));
  _74283 _74283_1 (
    .pin1(_74283_1_pin1), .pin2(_7486_1_pin6), .pin3(a_1_b), .pin4(_74283_1_pin4), .pin5(a_0_b),
    .pin6(_7486_1_pin3), .pin7(sub_b), .pin8(1'b0), .pin9(_74283_1_pin9), .pin10(_74283_1_pin10),
    .pin11(_7486_1_pin11), .pin12(a_3_b), .pin13(_74283_1_pin13), .pin14(a_2_b), .pin15(_7486_1_pin8),
    .pin16(1'b1));
  LED S_0 (.in(_74283_1_pin4));
  LED S_1 (.in(_74283_1_pin1));
  LED S_2 (.in(_74283_1_pin13));
  LED S_3 (.in(_74283_1_pin10));
  LED C_out (.in(_74283_1_pin9));
endmodule
